// Logisim project piped.circ as structural Verilog: 3 circuits, main circuit main
module main (
);

  wire Clock;
  wire [31:0] adder_1_out, bit_extender_1_out, if_id_1_out_4, if_id_1_out_5, mipsprogramrom_1_p2,
       multiplexer_1_out, PC_q, registerfile_1_p3, registerfile_1_p4;

  Multiplexer #(.width(32), .enable("false")) multiplexer_1 (
    .in0(adder_1_out), .out(multiplexer_1_out));  // open: in1, sel
  Register #(.width(32)) PC (.D(multiplexer_1_out), .Q(PC_q));  // open: en, clk, clr
  Adder #(.width(32)) adder_1 (.a(PC_q), .b(32'h4), .out(adder_1_out));  // open: cin, cout
  // MIPSProgramROM mipsprogramrom_1: pin names not known; wires that end beside it: PC_q, mipsprogramrom_1_p2
  IF_ID if_id_1 (
    .in_1(adder_1_out), .in_2(mipsprogramrom_1_p2), .out_4(if_id_1_out_4), .out_5(if_id_1_out_5),
    .Clock(Clock));
  // RegisterFile registerfile_1: pin names not known; wires that end beside it: if_id_1_out_5[25:21], if_id_1_out_5[20:16], registerfile_1_p3, registerfile_1_p4
  Bit_Extender #(.in_width(16), .out_width(32), .\type ("sign")) bit_extender_1 (.out(bit_extender_1_out));  // open: in
  ID_EX id_ex_1 (
    .Incremented_PC_write(if_id_1_out_4), .Register_read_data_1_write(registerfile_1_p3),
    .Register_read_data_2(registerfile_1_p4), .Immediate_field_write(bit_extender_1_out), .Clock(Clock));  // open: Incremented_PC_read, Register_read_data_1_write_2, Register_read_data_2_write, Immediate_field_write_2
endmodule

module IF_ID (
  input  [31:0] in_1,
  input  [31:0] in_2,
  input  Clock,
  output [31:0] out_4,
  output [31:0] out_5
);

  Register #(.width(32)) Incremented_PC (.D(in_1), .Q(out_4), .clk(Clock));  // open: en, clr
  Register #(.width(32)) Fetched_instruction (.D(in_2), .Q(out_5), .clk(Clock));  // open: en, clr
endmodule

module ID_EX (
  input  [31:0] Incremented_PC_write,
  input  [31:0] Register_read_data_1_write,
  input  [31:0] Register_read_data_2,
  input  [31:0] Immediate_field_write,
  input  Clock,
  output [31:0] Incremented_PC_read,
  output [31:0] Register_read_data_1_write_2,
  output [31:0] Register_read_data_2_write,
  output [31:0] Immediate_field_write_2
);

  Register #(.width(32)) Incremented_PC (
    .D(Incremented_PC_write), .Q(Incremented_PC_read), .clk(Clock));  // open: en, clr
  Register #(.width(32)) Register_read_data_1 (
    .D(Register_read_data_1_write), .Q(Register_read_data_1_write_2), .clk(Clock));  // open: en, clr
  Register #(.width(32)) u_Register_read_data_2 (
    .D(Register_read_data_2), .Q(Register_read_data_2_write), .clk(Clock));  // open: en, clr
  Register #(.width(32)) Immediate_field (
    .D(Immediate_field_write), .Q(Immediate_field_write_2), .clk(Clock));  // open: en, clr
endmodule
